// Logisim project processor.circ as structural Verilog
module ALU (
  input  [2:0] F,
  input  [31:0] B,
  input  [31:0] A,
  output [31:0] Y,
  output ZERO
);

  wire [31:0] adder_1_out, and_1_out, bit_extender_1_out, multiplexer_1_out, not_1_out, or_1_out;

  assign not_1_out = ~B;  // NOT_Gate not_1, 32 bits wide
  Multiplexer #(.width(32), .enable("false")) multiplexer_1 (
    .in0(B), .in1(not_1_out), .out(multiplexer_1_out), .sel(F[2]));
  Adder #(.width(32)) adder_1 (.a(multiplexer_1_out), .b(A), .out(adder_1_out), .cin(F[2]));  // open: cout
  assign and_1_out = multiplexer_1_out & A;  // AND_Gate and_1, 32 bits wide
  assign or_1_out = multiplexer_1_out | A;  // OR_Gate or_1, 32 bits wide
  assign bit_extender_1_out = {{31{1'b0}}, adder_1_out[31]};  // Bit_Extender bit_extender_1
  Multiplexer #(.select(2), .width(32), .enable("false")) multiplexer_2 (
    .in0(and_1_out), .in1(or_1_out), .in2(adder_1_out), .in3(bit_extender_1_out), .out(Y), .sel(F[1:0]));
  Comparator #(.width(32), .mode("unsigned")) comparator_1 (.a(Y), .b({32{1'b0}}), .eq(ZERO));  // open: gt, lt

  // Notes on the sheet:
  //   F 2
  //   A & B
  //   A | B
  //   ADD A B F(2) C_in
  //   zero extension for SLT
  //   This definitely works as intended, I promise*
  //   F 1:0
  //   if all bits of Y == 0, ZERO is 1
endmodule

module Datapath (
  output [31:0] v0
);

  wire clock_1_out;
  wire [7:0] register_1_q, shifter_1_out, undriven;

  Clock clock_1 (.out(clock_1_out));
  Register register_1 (.D(undriven), .Q(register_1_q), .clk(clock_1_out));  // open: en, clr
  Shifter #(.shift("lr")) shifter_1 (.in(register_1_q), .\dist (3'b010), .out(shifter_1_out));
  ROM #(.dataWidth(32)) rom_1 (.addr(shifter_1_out));  // open: data, sel
  ControlUnit controlunit_1 ();  // open: Instruction, RegDst, RegWrite, ALUControl, Branch, ALUSrc

  // Notes on the sheet:
  //   contents of rom_1 (hex, n*v repeats v):
  //   aa bbbbbbbb cc
endmodule

module Tests (
  output [31:0] Y,
  output [7:0] out_2,
  output [7:0] out_3,
  output [2:0] out_4
);

  BitSelector #(.width(32), .group(8)) bitselector_1 (.in(32'h12356789), .out(out_2), .sel(2'b01));
  BitSelector #(.width(32), .group(8)) bitselector_2 (.in(32'h12356789), .out(out_3), .sel(2'b01));
  BitSelector #(.group(3)) bitselector_3 (.in(out_3), .out(out_4), .sel(2'b00));

  assign Y = 32'hf4010207;

  // Notes on the sheet:
  //   binary values in Logisim. Convince yourself how the bits are displayed.
  //   Example 2: The bit selector is configured to have 32  
  //   bit group #1 (starting at index 0) is selected for the output.
  //   That is, the 8 bits 0x67 at bit indices 15..8  are sent to the output.
  //   Example 3: Now, assume that you want to extract 3 bits at   
  //   Example 1: A simple example that illustrates how 32-bit values are displayed as 
  //   input bits and 8 output bits. The parameter constant is 1, which means that   
  //   bit indices 10..8. This can be accoplished by putting two bit selecotrs in series.
endmodule

module RegisterFile (
  input  CLK,
  input  [2:0] A1,
  input  [31:0] WD3,
  input  [2:0] A2,
  input  WE3,
  input  [2:0] A3,
  output [31:0] RD1,
  output [31:0] RD2,
  output [31:0] V0
);

  wire and_1_out, and_2_out, and_3_out, and_4_out, and_5_out, and_6_out, and_7_out, and_8_out,
       decoder_1_out0, decoder_1_out1, decoder_1_out2, decoder_1_out3, decoder_1_out4, decoder_1_out5,
       decoder_1_out6, decoder_1_out7;
  wire [31:0] reg__0_q, register_1_q, register_2_q, register_3_q, register_4_q, register_5_q, register_6_q;

  Decoder #(.select(3)) decoder_1 (
    .out0(decoder_1_out0), .out1(decoder_1_out1), .out2(decoder_1_out2), .out3(decoder_1_out3),
    .out4(decoder_1_out4), .out5(decoder_1_out5), .out6(decoder_1_out6), .out7(decoder_1_out7), .sel(A3));  // open: en
  and and_1 (and_1_out, WE3, decoder_1_out0);
  and and_2 (and_2_out, WE3, decoder_1_out1);
  and and_3 (and_3_out, WE3, decoder_1_out2);
  and and_4 (and_4_out, WE3, decoder_1_out3);
  and and_5 (and_5_out, WE3, decoder_1_out4);
  and and_6 (and_6_out, WE3, decoder_1_out5);
  and and_7 (and_7_out, WE3, decoder_1_out6);
  and and_8 (and_8_out, WE3, decoder_1_out7);
  Register #(.width(32)) reg__0 (.D({32{1'b0}}), .en(and_1_out), .Q(reg__0_q), .clk(CLK));  // open: clr
  Register #(.width(32)) register_1 (.D(WD3), .en(and_2_out), .Q(register_1_q), .clk(CLK));  // open: clr
  Register #(.width(32)) u_v0 (.D(WD3), .en(and_3_out), .Q(V0), .clk(CLK));  // open: clr
  Register #(.width(32)) register_2 (.D(WD3), .en(and_4_out), .Q(register_2_q), .clk(CLK));  // open: clr
  Register #(.width(32)) register_3 (.D(WD3), .en(and_5_out), .Q(register_3_q), .clk(CLK));  // open: clr
  Register #(.width(32)) register_4 (.D(WD3), .en(and_6_out), .Q(register_4_q), .clk(CLK));  // open: clr
  Register #(.width(32)) register_5 (.D(WD3), .en(and_7_out), .Q(register_5_q), .clk(CLK));  // open: clr
  Register #(.width(32)) register_6 (.D(WD3), .en(and_8_out), .Q(register_6_q), .clk(CLK));  // open: clr
  Multiplexer #(.select(3), .width(32)) multiplexer_1 (
    .in0(reg__0_q), .in1(register_1_q), .in2(V0), .in3(register_2_q), .in4(register_3_q), .in5(register_4_q),
    .in6(register_5_q), .in7(register_6_q), .out(RD1), .sel(A1));  // open: en
  Multiplexer #(.select(3), .width(32)) multiplexer_2 (
    .in0(reg__0_q), .in1(register_1_q), .in2(V0), .in3(register_2_q), .in4(register_3_q), .in5(register_4_q),
    .in6(register_5_q), .in7(register_6_q), .out(RD2), .sel(A2));  // open: en

  // Notes on the sheet:
  //   $0 : 0
  //   $v0 : 2
  //   $at : 1
endmodule

module ControlUnit (
  input  [31:0] Instruction,
  output RegDst,
  output RegWrite,
  output ALUSrc,
  output Branch,
  output [2:0] ALUControl
);

  wire [5:0] bitselector_1_out;
  wire [31:0] shifter_1_out;

  Shifter #(.width(32), .shift("lr")) shifter_1 (.in(Instruction), .\dist (5'b11010), .out(shifter_1_out));
  BitSelector #(.width(32), .group(6)) bitselector_1 (.in(shifter_1_out), .out(bitselector_1_out), .sel(3'b000));
  Comparator #(.width(6), .mode("unsigned")) comparator_1 (
    .a(bitselector_1_out), .b(6'b001000), .eq(ALUSrc));  // open: gt, lt
  Comparator #(.width(6), .mode("unsigned")) comparator_2 (
    .a(bitselector_1_out), .b({6{1'b0}}), .eq(RegDst));  // open: gt, lt
  Comparator #(.width(6), .mode("unsigned")) comparator_3 (
    .a(bitselector_1_out), .b(6'b000100), .eq(Branch));  // open: gt, lt
  or or_1 (RegWrite, ALUSrc, RegDst);

  assign ALUControl = 3'b010;

  // Notes on the sheet:
  //   we assume that we can only do add if zero???
  //   and not another R-type function since no funct
  //   shift input 26 steps right
  //   SEL(6,0) -> send out group 0, the OPCODE 
  //   if opcode == 8, addi
  //   if opcode == 0, add (voodoo stuff)
  //   lista ut vad ALUcontrol beror på för bitvärden, ska det finnas en jämförelse innan eller bara två MUX:ar i serie?
endmodule
